# Fritzing sketch Untitled Sketch (saved by Fritzing 0.9.2b)
breadboards: 1

parts:
  Part1 = Arduino GSM Shield
  M1 = Stepper Motor - Bipolar
  VCC1 = Battery
  MD03A1 = Dual VNH2SP30 Motor Driver [part_number=MD03A]

nets:
  N1: Part1.AGND, VCC1.-, MD03A1.GND
  N2: Part1.MOSI/PWM_D11, MD03A1.2INb#143
  N3: Part1.SS/PWM_D10, MD03A1.2INb#142
  N4: Part1.PWM_D9, MD03A1.1INb
  N5: Part1.D8, MD03A1.1INa
  5V: Part1.5V, MD03A1.VIN
  N6: Part1.VIN, VCC1.+
  N7: M1.D, MD03A1.OUT_2B
